// Digital circuit DUX1a4_4bit.dig as structural Verilog
module DUX1a4_4bit (
  input  B,
  input  A,
  input  [3:0] D,
  output [3:0] I0,
  output [3:0] I1,
  output [3:0] I2,
  output [3:0] I3
);

  DUX1a4_1bit DUX0 (.A(B), .B(A), .D(D[0]), .I0(I0[0]), .I1(I1[0]), .I2(I2[0]), .I3(I3[0]));
  DUX1a4_1bit DUX1 (.A(B), .B(A), .D(D[1]), .I0(I0[1]), .I1(I1[1]), .I2(I2[1]), .I3(I3[1]));
  DUX1a4_1bit DUX2 (.A(B), .B(A), .D(D[2]), .I0(I0[2]), .I1(I1[2]), .I2(I2[2]), .I3(I3[2]));
  DUX1a4_1bit DUX3 (.A(B), .B(A), .D(D[3]), .I0(I0[3]), .I1(I1[3]), .I2(I2[3]), .I3(I3[3]));

  // Notes on the sheet:
  //   Demultiplexor 1 a 4 de 4bits
endmodule
