// Digital circuit DUX1a4_8bit.dig as structural Verilog
module DUX1a4_8bit (
  input  A,
  input  B,
  input  [7:0] D,
  output [7:0] I0,
  output [7:0] I1,
  output [7:0] I2,
  output [7:0] I3
);

  DUX1a4_4bit dux1a4_4bit_1 (.B(B), .A(A), .D(D[3:0]), .I0(I0[3:0]), .I1(I1[3:0]), .I2(I2[3:0]), .I3(I3[3:0]));
  DUX1a4_4bit dux1a4_4bit_2 (.B(B), .A(A), .D(D[7:4]), .I0(I0[7:4]), .I1(I1[7:4]), .I2(I2[7:4]), .I3(I3[7:4]));
  // Pins of 1 and 8 bits meet at I0
  // Pins of 1 and 8 bits meet at I1
  // Pins of 1 and 8 bits meet at I2
  // Pins of 1 and 8 bits meet at I3
endmodule
