// Digital circuit MUX4a1_1bit.dig as structural Verilog
module MUX4a1_1bit (
  input  I0,
  input  S0,
  input  S1,
  input  I1,
  input  I2,
  input  I3,
  output Y
);

  wire and_1_out, and_2_out, and_3_out, and_4_out, not_1_out, not_2_out;

  not not_1 (not_1_out, S0);
  not not_2 (not_2_out, S1);
  and and_1 (and_1_out, I3, S0, S1);
  and and_2 (and_2_out, I2, not_1_out, S1);
  and and_3 (and_3_out, I1, S0, not_2_out);
  and and_4 (and_4_out, I0, not_1_out, not_2_out);
  or or_1 (Y, and_1_out, and_2_out, and_3_out, and_4_out);

  // Notes on the sheet:
  //   S0'
  //   S1'
  //   S0
  //   S1
  //   Multiplexor 4 a 1 x 1bit
endmodule
