// Digital circuit MUX4a1_8bit.dig as structural Verilog
module MUX4a1_8bit (
  input  S0,
  input  S1,
  input  [7:0] I0,
  input  [7:0] I1,
  input  [7:0] I2,
  input  [7:0] I3,
  output [7:0] Y
);

  MUX4a1_4bit mux4a1_4bit_1 (.S0(S0), .S1(S1), .I0(I0[3:0]), .I1(I1[3:0]), .I2(I2[3:0]), .I3(I3[3:0]), .Y(Y[3:0]));
  MUX4a1_4bit mux4a1_4bit_2 (.S0(S0), .S1(S1), .I0(I0[7:4]), .I1(I1[7:4]), .I2(I2[7:4]), .I3(I3[7:4]), .Y(Y[7:4]));

  // Notes on the sheet:
  //   Muliplexor 4 a 1 de 8bits
endmodule
