// Digital circuit TallerNo3CircuitoOriginal.dig as structural Verilog
module TallerNo3CircuitoOriginal (
  input  X,
  input  Y,
  input  Z,
  output S,
  output C
);

  wire and_1_out, and_2_out, and_3_out, and_4_out, and_5_out, and_6_out, and_7_out, not_1_out, not_2_out,
       not_3_out, or_1_out, or_2_out, or_3_out, or_4_out;

  not not_1 (not_1_out, X);
  not not_2 (not_2_out, Y);
  not not_3 (not_3_out, Z);
  and and_1 (and_1_out, not_1_out, not_2_out, Z);
  and and_2 (and_2_out, not_1_out, Y, not_3_out);
  and and_3 (and_3_out, X, not_2_out, not_3_out);
  and and_4 (and_4_out, X, Y, Z);
  and and_5 (and_5_out, not_1_out, Y, Z);
  and and_6 (and_6_out, X, not_2_out, Z);
  and and_7 (and_7_out, X, Y, not_3_out);
  or or_1 (or_1_out, and_1_out, and_2_out);
  or or_2 (or_2_out, and_3_out, and_4_out);
  or or_3 (or_3_out, and_4_out, and_5_out);
  or or_4 (or_4_out, and_6_out, and_7_out);
  or or_5 (S, or_1_out, or_2_out);
  or or_6 (C, or_3_out, or_4_out);

  // Notes on the sheet:
  //   X
  //   Y
  //   X'
  //   Y'
  //   Z
  //   Z'
  //   Circuito Original:
  //   X' Y' Z
  //   X' Y Z'
  //   X Y' Z'
  //   X Y Z
  //   X' Y Z
  //   X Y' Z
  //   X Y Z'
  //   (X' Y' Z) +
  //   (X' Y Z')
  //   (X Y' Z') +
  //   (X Y Z)
  //   (X Y Z) +
  //   (X' Y Z)
  //   (X Y' Z) +
  //   (X Y Z')
  //   (X' Y' Z) +
  //   (X' Y Z') 
  //   +
  //   (X Y' Z') +
  //   (X Y Z)
  //   (X Y Z) +
  //   (X' Y Z) 
  //   +
  //   (X Y' Z) +
  //   (X Y Z')
  //   =   (X' Y' Z) + (X' Y Z') + (X Y' Z') + (X Y Z)
  //   => X' [(Y' Z) + (Y Z')] + X [(Y' Z') + (Y Z)]
  //   => X' (Y ^ Z) + X (Y ^ Z)'
  //   => X ^ Y ^ Z
  //   = (X Y Z) + (X' Y Z) + (X Y' Z) + (X Y Z')
  //   => (X Y Z) + (X Y Z')  + (X' Y Z) + (X Y' Z)
  //   => X Y (Z + Z') +  Z [(X' Y) + (X Y')]
  //   => X Y (1) + Z (X + Y)
  //   => X Y + X Z + Y Z
endmodule
