// Digital circuit TallerNo3CircuitoSimplificado.dig as structural Verilog
module TallerNo3CircuitoSimplificado (
  input  X,
  input  Y,
  input  Z,
  output S,
  output C
);

  wire and_1_out, and_2_out, and_3_out;

  xor xor_1 (S, X, Y, Z);
  and and_1 (and_1_out, X, Y);
  and and_2 (and_2_out, X, Z);
  and and_3 (and_3_out, Y, Z);
  or or_1 (C, and_1_out, and_2_out, and_3_out);

  // Notes on the sheet:
  //   X
  //   Y
  //   Z
  //   Circuito Simplificado
  //   X ^ Y ^ Z
  //   X Y
  //   X Z
  //   Y Z
  //   X Y + X Z + Y Z
  //   = X ^ Y ^ Z
  //   = X Y + X Z + Y Z
endmodule
