// Digital circuit FlipFlopD_NoCLKyCLK.dig as structural Verilog
module FlipFlopD_NoCLKyCLK (
  input  D,
  input  D_2,
  input  CLK,
  output Q1,
  output Q1_2,
  output Q2,
  output Q1_3
);

  wire nand_1_out, not_1_out, not_2_out;

  not not_1 (not_1_out, D);
  nor nor_1 (Q1, not_1_out, Q1_2);
  nor nor_2 (Q1_2, Q1, D);
  nand nand_1 (nand_1_out, D_2, CLK);
  not not_2 (not_2_out, nand_1_out);
  nor nor_3 (Q2, not_2_out, Q1_3);
  nor nor_4 (Q1_3, Q2, nand_1_out);

  // Notes on the sheet:
  //   FlipFlop D Sin Reloj
  //   FlipFlop D
endmodule
