// Digital circuit FlipFlopJK.dig as structural Verilog
module FlipFlopJK (
  input  J,
  input  K,
  input  CLK,
  output Q,
  output Q_2
);

  wire nand_1_out, nand_2_out, undriven, undriven_2;

  nand nand_1 (nand_1_out, undriven, J, CLK);
  nand nand_2 (nand_2_out, CLK, K, undriven_2);
  nor nor_1 (Q, nand_1_out, undriven_2);
  nor nor_2 (Q_2, undriven, nand_2_out);

  // Notes on the sheet:
  //   FlipFlop JK
endmodule
