// Digital circuit LatchSR_NANDyNOR.dig as structural Verilog
module LatchSR_NANDyNOR (
  input  S0,
  input  R0,
  input  S1,
  input  R2,
  output Q,
  output Q_2,
  output Q1,
  output Q1_2
);

  nand nand_1 (Q, S0, Q_2);
  nand nand_2 (Q_2, Q, R0);
  nor nor_1 (Q1, S1, Q1_2);
  nor nor_2 (Q1_2, Q1, R2);

  // Notes on the sheet:
  //   Latch SR NAND
  //   Latch SR NOR
endmodule
