// Digital circuit Res4bit.dig as structural Verilog
module Res4bit (
  input  [3:0] A,
  input  [3:0] B,
  input  Bin,
  output [3:0] D,
  output [3:0] Bout
);

  wire [3:0] not_1_out, sum4bit_1_p5;

  assign not_1_out = ~B;  // Not not_1, 4 bits wide
  // Sum4bit sum4bit_1: pin names not known; wires that end beside it: A, not_1_out, Bin, D, sum4bit_1_p5
  assign Bout = ~sum4bit_1_p5;  // Not not_2, 4 bits wide
  // Pins of 1 and 4 bits meet at Bout

  // Notes on the sheet:
  //   Restador de 4 bits
endmodule
