// Digital circuit Sum4bit.dig as structural Verilog
module Sum4bit (
  input  [3:0] A,
  input  [3:0] B,
  input  Cin,
  output [3:0] S,
  output Cout
);

  wire sumcom_1_cout, sumcom_2_cout, sumcom_3_cout;

  SumCom sumcom_1 (.A(A[0]), .B(B[0]), .Cin(Cin), .S(S[0]), .Cout(sumcom_1_cout));
  SumCom sumcom_2 (.A(A[1]), .B(B[1]), .Cin(sumcom_1_cout), .S(S[1]), .Cout(sumcom_2_cout));
  SumCom sumcom_3 (.A(A[2]), .B(B[2]), .Cin(sumcom_2_cout), .S(S[2]), .Cout(sumcom_3_cout));
  SumCom sumcom_4 (.A(A[3]), .B(B[3]), .Cin(sumcom_3_cout), .S(S[3]), .Cout(Cout));

  // Notes on the sheet:
  //   Sumador de 4bits
endmodule
