// Digital circuit ALU_32bit.dig as structural Verilog
module ALU_32bit (
  input  [31:0] arg1,
  input  [31:0] arg2,
  input  [2:0] Funtion3,
  input  Funtion7,
  output [31:0] Out
);

  wire [0:0] slt, stlu;
  wire [31:0] add, \and , multiplexer_1_out, multiplexer_2_out, \or , sll, sra, srl, sub, \xor ;

  Add #(.Bits(32)) add_1 (.a(arg1), .b(arg2), .c_i(1'b0), .s(add));  // open: c_o
  Sub #(.Bits(32)) sub_1 (.a(arg1), .b(arg2), .c_i(1'b0), .s(sub));  // open: c_o
  assign \xor  = arg1 ^ arg2;  // XOr xor_1, 32 bits wide
  assign \or  = arg1 | arg2;  // Or or_1, 32 bits wide
  assign \and  = arg1 & arg2;  // And and_1, 32 bits wide
  BarrelShifter #(.Bits(32)) u_sll (.in(arg1), .shift({1'b0, arg2[4:0]}), .out(sll));
  BarrelShifter #(.Bits(32)) u_srl (.in(arg1), .shift({1'b0, arg2[4:0]}), .out(srl));
  BarrelShifter #(.Bits(32), .barrelSigned("true")) u_sra (.in(arg1), .shift({2'b00, arg2[4:0]}), .out(sra));
  Comparator #(.Bits(32)) u_slt (.a(arg1), .b(arg2), .lt(slt[0]));  // open: gt, eq
  Comparator #(.Bits(32)) sltu (.a(arg1), .b(arg2), .lt(stlu[0]));  // open: gt, eq
  Multiplexer #(.Bits(32)) multiplexer_1 (.sel(Funtion7), .in_0(add), .in_1(sub), .out(multiplexer_1_out));
  Multiplexer #(.Bits(32)) multiplexer_2 (.sel(Funtion7), .in_0(sra), .in_1(srl), .out(multiplexer_2_out));
  Multiplexer #(.Selector_Bits(3), .Bits(32)) multiplexer_3 (
    .sel(Funtion3), .in_0(multiplexer_1_out), .in_1(sll), .in_2({{31{1'b0}}, slt[0]}),
    .in_3({{31{1'b0}}, stlu[0]}), .in_4(\xor ), .in_5(multiplexer_2_out), .in_6(\or ), .in_7(\and ), .out(Out));
  // Probe bin on Out
  // Probe dec on Out
  // Probe hex on Out

  // Other names for the same wires on the sheet: f3[2:0] = Funtion3; f9 = Funtion7
endmodule
