// Digital circuit Branch_32bit.dig as structural Verilog
module Branch_32bit (
  input  UbrInst,
  input  [2:0] Function3,
  input  BrInst,
  input  [31:0] R2Data,
  input  [31:0] R1Data,
  output PC_Jump,
  output RS1_PC,
  output Equal,
  output LessThan,
  output GreatOrEqual,
  output LessThanU,
  output GreatOrEqualU
);

  wire and_1_out, and_2_out, and_3_out, and_4_out, and_5_out, and_6_out, Beq_eq, Bge_eq, Blt_eq, Bltu_2_eq,
       Bltu_eq, Bne_eq, EqualU, GreaterThan, GreaterThanU, multiplexer_1_out, multiplexer_2_out,
       multiplexer_3_out, multiplexer_4_out, multiplexer_5_out, multiplexer_6_out, NotEqual;

  or or_1 (GreatOrEqual, Equal, GreaterThan);
  not not_1 (NotEqual, Equal);
  or or_2 (GreatOrEqualU, EqualU, GreaterThanU);
  Comparator #(.Bits(32)) comparator_1 (.a(R1Data), .b(R2Data), .gt(GreaterThanU), .eq(EqualU), .lt(LessThanU));
  Comparator #(.Bits(32)) comparator_2 (.a(R1Data), .b(R2Data), .gt(GreaterThan), .eq(Equal), .lt(LessThan));
  Comparator #(.Bits(3)) Bltu (.a(3'b111), .b(Function3), .eq(Bltu_eq));  // open: gt, lt
  and and_1 (and_1_out, GreatOrEqualU, Bltu_eq);
  Multiplexer multiplexer_1 (.sel(and_1_out), .in_0(1'b0), .in_1(1'b1), .out(multiplexer_1_out));
  Comparator #(.Bits(3)) Bltu_2 (.a(3'b110), .b(Function3), .eq(Bltu_2_eq));  // open: gt, lt
  and and_2 (and_2_out, LessThanU, Bltu_2_eq);
  Multiplexer multiplexer_2 (.sel(and_2_out), .in_0(multiplexer_1_out), .in_1(1'b1), .out(multiplexer_2_out));
  Comparator #(.Bits(3)) Bge (.a(3'b101), .b(Function3), .eq(Bge_eq));  // open: gt, lt
  and and_3 (and_3_out, GreatOrEqual, Bge_eq);
  Comparator #(.Bits(3)) Blt (.a(3'b100), .b(Function3), .eq(Blt_eq));  // open: gt, lt
  Multiplexer multiplexer_3 (.sel(and_3_out), .in_0(multiplexer_2_out), .in_1(1'b1), .out(multiplexer_3_out));
  and and_4 (and_4_out, LessThan, Blt_eq);
  Multiplexer multiplexer_4 (.sel(and_4_out), .in_0(multiplexer_3_out), .in_1(1'b1), .out(multiplexer_4_out));
  Comparator #(.Bits(3)) Bne (.a(3'b001), .b(Function3), .eq(Bne_eq));  // open: gt, lt
  and and_5 (and_5_out, NotEqual, Bne_eq);
  Multiplexer multiplexer_5 (.sel(and_5_out), .in_0(multiplexer_4_out), .in_1(1'b1), .out(multiplexer_5_out));
  Comparator #(.Bits(3)) Beq (.a(3'b000), .b(Function3), .eq(Beq_eq));  // open: gt, lt
  and and_6 (and_6_out, Equal, Beq_eq);
  Multiplexer multiplexer_6 (.sel(and_6_out), .in_0(multiplexer_5_out), .in_1(1'b1), .out(multiplexer_6_out));
  and and_7 (RS1_PC, multiplexer_6_out, BrInst);
  or or_3 (PC_Jump, RS1_PC, UbrInst);

  // Other names for the same wires on the sheet: GreaterOrEqual = GreatOrEqual; GreaterOrEqualU = GreatOrEqualU;
  //   Type[2:0] = Function3

  // Notes on the sheet:
  //   Branch de 32Bits
endmodule
