// Digital circuit CU_32bits.dig as structural Verilog
module CU_32bits (
  input  [31:0] Instruction,
  output [6:0] ImmediateRegister,
  output DMwrEnable,
  output JAL___JALR,
  output [1:0] WBSel,
  output Store,
  output Load,
  output Branch,
  output RegisterFileEnable,
  output SRAI___Sub,
  output Function3,
  output [6:0] Function7,
  output [6:0] OpCode
);

  wire deco_32bit_1_p3, Imm_eq, JAL_eq, JALR_eq, Load_eq, or_2_out;
  wire [1:0] multiplexer_1_out;
  wire [1:1] undriven, undriven_2;
  wire [6:0] R_eq;

  // Deco_32bit deco_32bit_1: pin names not known; wires that end beside it: Instruction, OpCode, deco_32bit_1_p3, Function7
  Comparator #(.Bits(7)) R (.a(OpCode), .b(7'b0110011), .eq(R_eq[0]));  // open: gt, lt
  Comparator #(.Bits(7)) Imm (.a(OpCode), .b(7'b0010011), .eq(Imm_eq));  // open: gt, lt
  Comparator #(.Bits(7)) S (.a(OpCode), .b(7'b0100011), .eq(DMwrEnable));  // open: gt, lt
  Comparator #(.Bits(7)) u_Load (.a(OpCode), .b(7'b0000011), .eq(Load_eq));  // open: gt, lt
  Comparator #(.Bits(7)) JAL (.a(OpCode), .b(7'b1101111), .eq(JAL_eq));  // open: gt, lt
  Comparator #(.Bits(7)) JALR (.a(OpCode), .b(7'b1100111), .eq(JALR_eq));  // open: gt, lt
  Comparator #(.Bits(7)) u_Store (.a(OpCode), .b(7'b0100011), .eq(Store));  // open: gt, lt
  Comparator #(.Bits(7)) Load_2 (.a(OpCode), .b(7'b0000011), .eq(Load));  // open: gt, lt
  Comparator #(.Bits(7)) u_Branch (.a(OpCode), .b(7'b1100011), .eq(Branch));  // open: gt, lt
  assign ImmediateRegister = ~R_eq;  // Not not_1, 7 bits wide
  or or_1 (JAL___JALR, JAL_eq, JALR_eq);
  or or_2 (or_2_out, Branch, R_eq[0], Imm_eq);
  Multiplexer #(.Bits(2)) multiplexer_1 (
    .sel(JAL___JALR), .in_0({undriven[1], 1'b0}), .in_1(2'b10), .out(multiplexer_1_out));
  Multiplexer #(.Bits(2)) multiplexer_2 (
    .sel(Load_eq), .in_0({undriven_2[1], 1'b0}), .in_1(multiplexer_1_out), .out(WBSel));
  Multiplexer multiplexer_3 (.sel(or_2_out), .in_0(Function7[4]), .in_1(1'b0), .out(SRAI___Sub));
  Multiplexer multiplexer_4 (.sel(Branch), .in_0(deco_32bit_1_p3), .in_1(1'b0), .out(Function3));
  or or_3 (RegisterFileEnable, R_eq[0], Imm_eq, JAL___JALR, Load);
  // Pins of 1 and 7 bits meet at OpCode
  // Pins of 1 and 7 bits meet at R_eq
  // Pins of 1 and 7 bits meet at ImmediateRegister
  // Pins of 1 and 2 bits meet at {undriven[1], 1'b0}
  // Pins of 1 and 2 bits meet at {undriven_2[1], 1'b0}
  // Pins of 1 and 2 bits meet at WBSel
  // Pins of 1 and 7 bits meet at Function7
endmodule
