// Digital circuit DataMemory_32bits.dig as structural Verilog
module DataMemory_32bits (
  input  [31:0] WData,
  input  Clock,
  input  DMwrEna,
  input  [2:0] Function3,
  input  [31:0] RWAdress,
  output [31:0] DataRD
);

  wire and_1_out, and_2_out, and_3_out, and_4_out, Byte, Byte_0, Byte_1, Byte_2, ByteU, Half, HalfU;
  wire [7:0] Byte_0_d, Byte_1_d, Byte_2_d, Byte_3_d, multiplexer_1_out, multiplexer_2_out, multiplexer_3_out,
       multiplexer_4_out;
  wire [31:0] bitextender_1_out, bitextender_2_out, multiplexer_5_out, multiplexer_6_out, multiplexer_7_out,
       multiplexer_8_out, notconnected_1_out;

  Comparator #(.Bits(3)) comparator_1 (.a(3'b101), .b(Function3), .eq(HalfU));  // open: gt, lt
  Comparator #(.Bits(3)) comparator_2 (.a(3'b100), .b(Function3), .eq(ByteU));  // open: gt, lt
  Comparator #(.Bits(3)) comparator_3 (.a(3'b010), .b(Function3), .eq(Byte_2));  // open: gt, lt
  Comparator #(.Bits(3)) comparator_4 (.a(3'b001), .b(Function3), .eq(Half));  // open: gt, lt
  Comparator #(.Bits(3)) comparator_5 (.a(3'b000), .b(Function3), .eq(Byte));  // open: gt, lt
  and and_1 (and_1_out, DMwrEna, Byte_0);
  BlockRAMDualPort #(.AddrBits(16), .Bits(8)) u_Byte_0 (
    .A(RWAdress[15:0]), .Din(WData[7:0]), .str(and_1_out), .C(Clock), .D(Byte_0_d));
  or or_1 (Byte_0, Byte, Half, Byte_2);
  or or_2 (Byte_1, Half, Byte_2);
  and and_2 (and_2_out, DMwrEna, Byte_1);
  BlockRAMDualPort #(.AddrBits(16), .Bits(8)) u_Byte_1 (
    .A(RWAdress[15:0]), .Din(WData[15:8]), .str(and_2_out), .C(Clock), .D(Byte_1_d));
  and and_3 (and_3_out, DMwrEna, Byte_2);
  BlockRAMDualPort #(.AddrBits(16), .Bits(8)) u_Byte_2 (
    .A(RWAdress[15:0]), .Din(WData[23:16]), .str(and_3_out), .C(Clock), .D(Byte_2_d));
  and and_4 (and_4_out, DMwrEna, Byte_2);
  BlockRAMDualPort #(.AddrBits(16), .Bits(8)) Byte_3 (
    .A(RWAdress[15:0]), .Din(WData[31:24]), .str(and_4_out), .C(Clock), .D(Byte_3_d));
  Multiplexer #(.Bits(8)) multiplexer_1 (.sel(Byte_0), .in_0({8{1'b0}}), .in_1(Byte_0_d), .out(multiplexer_1_out));
  Multiplexer #(.Bits(8)) multiplexer_2 (.sel(Byte_1), .in_0({8{1'b0}}), .in_1(Byte_1_d), .out(multiplexer_2_out));
  Multiplexer #(.Bits(8)) multiplexer_3 (.sel(Byte_2), .in_0({8{1'b0}}), .in_1(Byte_2_d), .out(multiplexer_3_out));
  Multiplexer #(.Bits(8)) multiplexer_4 (.sel(Byte_2), .in_0({8{1'b0}}), .in_1(Byte_3_d), .out(multiplexer_4_out));
  // Probe on multiplexer_1_out
  // Probe on multiplexer_2_out
  // Probe on multiplexer_3_out
  // Probe on multiplexer_4_out
  BitExtender #(.inputBits(16), .outputBits(32)) bitextender_1 (
    .in({multiplexer_2_out, multiplexer_1_out}), .out(bitextender_1_out));
  BitExtender #(.outputBits(32)) bitextender_2 (.in(multiplexer_1_out), .out(bitextender_2_out));
  Multiplexer #(.Bits(32)) multiplexer_5 (
    .sel(ByteU), .in_0(notconnected_1_out), .in_1({{24{1'b0}}, multiplexer_1_out}), .out(multiplexer_5_out));
  // NotConnected on notconnected_1_out
  Multiplexer #(.Bits(32)) multiplexer_6 (
    .sel(HalfU), .in_0(multiplexer_5_out), .in_1({{16{1'b0}}, multiplexer_2_out, multiplexer_1_out}),
    .out(multiplexer_6_out));
  Multiplexer #(.Bits(32)) multiplexer_7 (
    .sel(Byte_2), .in_0(multiplexer_6_out),
    .in_1({multiplexer_4_out, multiplexer_3_out, multiplexer_2_out, multiplexer_1_out}),
    .out(multiplexer_7_out));
  Multiplexer #(.Bits(32)) multiplexer_8 (
    .sel(Half), .in_0(multiplexer_7_out), .in_1(bitextender_1_out), .out(multiplexer_8_out));
  Multiplexer #(.Bits(32)) multiplexer_9 (.sel(Byte), .in_0(multiplexer_8_out), .in_1(bitextender_2_out), .out(DataRD));

  // Other names for the same wires on the sheet: DMWen = DMwrEna; Data_0[7:0] = WData[7:0]; Data_1[7:0] = WData[15:8];
  //   Data_2[7:0] = WData[23:16]; Data_3[7:0] = WData[31:24]; Byte_3 = Byte_2; Word = Byte_2
endmodule
