// Digital circuit Immediate_32bits.dig as structural Verilog
module Immediate_32bits (
  input  [31:0] Instruction,
  output [31:0] Immediate
);

  wire and_1_out, inst_case_1_typeb, inst_case_1_typei, inst_case_1_typeijal, inst_case_1_typeiload,
       inst_case_1_typeishift, inst_case_1_typej, inst_case_1_types, inst_case_1_typeuauipc,
       inst_case_1_typeului, or_1_out, or_2_out;
  wire [31:0] B_Immediate, I_Immediate, I_Shamt, J_Immediate, multiplexer_1_out, multiplexer_2_out,
       multiplexer_3_out, multiplexer_4_out, multiplexer_5_out, S_Immediate, U_Immediate;

  Inst_Decoder_I inst_decoder_i_1 (
    .Instruction(Instruction), .Immediate(I_Immediate), .Shamt(I_Shamt));  // open: srai_srli
  Inst_Decoder_S inst_decoder_s_1 (.Instruction(Instruction), .Immediate(S_Immediate));
  // Inst_Decoder_B inst_decoder_b_1: pin names not known; wires that end beside it: Instruction, B_Immediate
  Inst_Decoder_J inst_decoder_j_1 (.Instruction(Instruction), .Immediate(J_Immediate));
  Inst_Decoder_U inst_decoder_u_1 (.Instruction(Instruction), .Immediate(U_Immediate));
  Inst_Case inst_case_1 (
    .Instruction(Instruction), .TypeI(inst_case_1_typei), .TypeILoad(inst_case_1_typeiload),
    .TypeS(inst_case_1_types), .TypeB(inst_case_1_typeb), .TypeJ(inst_case_1_typej),
    .TypeIJAL(inst_case_1_typeijal), .TypeULUI(inst_case_1_typeului), .TypeUAUIPC(inst_case_1_typeuauipc),
    .TypeIShift(inst_case_1_typeishift));  // open: TypeR, TypeIE
  or or_1 (or_1_out, inst_case_1_typeului, inst_case_1_typeuauipc);
  Multiplexer #(.Bits(32)) multiplexer_1 (
    .sel(or_1_out), .in_0({32{1'b0}}), .in_1(U_Immediate), .out(multiplexer_1_out));
  Multiplexer #(.Bits(32)) multiplexer_2 (
    .sel(inst_case_1_typej), .in_0(multiplexer_1_out), .in_1(J_Immediate), .out(multiplexer_2_out));
  Multiplexer #(.Bits(32)) multiplexer_3 (
    .sel(inst_case_1_typeb), .in_0(multiplexer_2_out), .in_1(B_Immediate), .out(multiplexer_3_out));
  Multiplexer #(.Bits(32)) multiplexer_4 (
    .sel(inst_case_1_types), .in_0(multiplexer_3_out), .in_1(S_Immediate), .out(multiplexer_4_out));
  or or_2 (or_2_out, inst_case_1_typei, inst_case_1_typeijal, inst_case_1_typeiload);
  Multiplexer #(.Bits(32)) multiplexer_5 (
    .sel(or_2_out), .in_0(multiplexer_4_out), .in_1(I_Immediate), .out(multiplexer_5_out));
  and and_1 (and_1_out, inst_case_1_typei, inst_case_1_typeishift);
  Multiplexer #(.Bits(32)) multiplexer_6 (.sel(and_1_out), .in_0(multiplexer_5_out), .in_1(I_Shamt), .out(Immediate));
endmodule
