// Digital circuit Inst-Case.dig as structural Verilog
module Inst_Case (
  input  [31:0] Instruction,
  output TypeR,
  output TypeI,
  output TypeIE,
  output TypeILoad,
  output TypeS,
  output TypeB,
  output TypeJ,
  output TypeIJAL,
  output TypeULUI,
  output TypeUAUIPC,
  output TypeIShift
);

  wire comparator_1_eq, comparator_2_eq, or_1_out;

  Comparator #(.Bits(3)) comparator_1 (.a(Instruction[14:12]), .b(3'b101), .eq(comparator_1_eq));  // open: gt, lt
  Comparator #(.Bits(3)) comparator_2 (.a(Instruction[14:12]), .b(3'b001), .eq(comparator_2_eq));  // open: gt, lt
  or or_1 (or_1_out, comparator_1_eq, comparator_2_eq);
  and and_1 (TypeIShift, TypeI, or_1_out);
  Comparator #(.Bits(7)) comparator_3 (.a(7'b0110011), .b(Instruction[6:0]), .eq(TypeR));  // open: gt, lt
  Comparator #(.Bits(7)) comparator_4 (.a(7'b0010011), .b(Instruction[6:0]), .eq(TypeI));  // open: gt, lt
  Comparator #(.Bits(7)) comparator_5 (.a(7'b1110011), .b(Instruction[6:0]), .eq(TypeIE));  // open: gt, lt
  Comparator #(.Bits(7)) comparator_6 (.a(7'b0000011), .b(Instruction[6:0]), .eq(TypeILoad));  // open: gt, lt
  Comparator #(.Bits(7)) comparator_7 (.a(7'b0100011), .b(Instruction[6:0]), .eq(TypeS));  // open: gt, lt
  Comparator #(.Bits(7)) comparator_8 (.a(7'b1100011), .b(Instruction[6:0]), .eq(TypeB));  // open: gt, lt
  Comparator #(.Bits(7)) comparator_9 (.a(7'b1101111), .b(Instruction[6:0]), .eq(TypeJ));  // open: gt, lt
  Comparator #(.Bits(7)) comparator_10 (.a(7'b1100111), .b(Instruction[6:0]), .eq(TypeIJAL));  // open: gt, lt
  Comparator #(.Bits(7)) comparator_11 (.a(7'b0110111), .b(Instruction[6:0]), .eq(TypeULUI));  // open: gt, lt
  Comparator #(.Bits(7)) comparator_12 (.a(7'b0010111), .b(Instruction[6:0]), .eq(TypeUAUIPC));  // open: gt, lt

  // Other names for the same wires on the sheet: F3[2:0] = Instruction[14:12]; F7[6:0] = Instruction[31:25];
  //   TISO = TypeIShift; TypeIS = TypeI
endmodule
