// Digital circuit Inst_Decoder_I.dig as structural Verilog
module Inst_Decoder_I (
  input  [31:0] Instruction,
  output [31:0] Immediate,
  output [31:0] Shamt,
  output srai_srli
);

  BitExtender #(.inputBits(1), .outputBits(20)) bitextender_1 (.in(Instruction[31]), .out(Immediate[31:12]));

  assign Immediate[11:0] = Instruction[31:20];
  assign Shamt = {{27{1'b0}}, Instruction[24:20]};
  assign srai_srli = Instruction[30];
endmodule
