// Digital circuit Inst_Decoder_J.dig as structural Verilog
module Inst_Decoder_J (
  input  [31:0] Instruction,
  output [31:0] Immediate
);

  BitExtender #(.inputBits(1), .outputBits(11)) bitextender_1 (.in(Instruction[31]), .out(Immediate[31:21]));

  assign Immediate[20:0] = {Instruction[31], Instruction[19:12], Instruction[20], Instruction[30:21], 1'b0};
endmodule
