// Digital circuit ProcesadorMonociclo_32bits.dig as structural Verilog
module ProcesadorMonociclo_32bits (
  input  Clock,
  input  Reset
);

  wire branch_32bit_1_pc_jump, branch_32bit_1_rs1_pc, cu_32bits_1_branch, cu_32bits_1_jal___jalr, DMwrEn,
       ImmReg, RFwrEnable, SRAI_SUB;
  wire [1:0] WBSel;
  wire [2:0] Function3;
  wire [4:0] pm24_32bit_1_inst_2, pm24_32bit_1_inst_3, pm24_32bit_1_inst_4;
  wire [6:0] Function7;
  wire [31:0] add_1_s, alu_32bit_1_out, datamemory_32bits_1_datard, immediate_32bits_1_immediate,
       multiplexer_1_out, multiplexer_2_out, multiplexer_3_out, multiplexer_4_out, notconnected_1_out,
       pc_32bit_1_output, pm24_32bit_1_inst, rf24_32bit_1_rs1data, WData;

  PC_32bit pc_32bit_1 (
    .Input(multiplexer_3_out), .Clock(Clock), .WriteEnable(1'b1), .Reset(Reset), .Output(pc_32bit_1_output));
  // Probe on Function3
  // Probe on Function7
  Add #(.Bits(32)) add_1 (.a(32'h4), .b(pc_32bit_1_output), .c_i(1'b0), .s(add_1_s));  // open: c_o
  PM24_32bit pm24_32bit_1 (
    .Addres(pc_32bit_1_output),
    .Inst({pm24_32bit_1_inst[31:25], pm24_32bit_1_inst_4, pm24_32bit_1_inst_3, pm24_32bit_1_inst[14:12], pm24_32bit_1_inst_2, pm24_32bit_1_inst[6:0]}));
  CU_32bits cu_32bits_1 (
    .Instruction({pm24_32bit_1_inst[31:25], pm24_32bit_1_inst_4, pm24_32bit_1_inst_3, pm24_32bit_1_inst[14:12], pm24_32bit_1_inst_2, pm24_32bit_1_inst[6:0]}),
    .ImmediateRegister(ImmReg), .DMwrEnable(DMwrEn), .JAL___JALR(cu_32bits_1_jal___jalr), .WBSel(WBSel),
    .Branch(cu_32bits_1_branch), .RegisterFileEnable(RFwrEnable), .SRAI___Sub(SRAI_SUB),
    .Function3(Function3), .Function7(Function7));  // open: Store, Load, OpCode
  Immediate_32bits immediate_32bits_1 (
    .Instruction({pm24_32bit_1_inst[31:25], pm24_32bit_1_inst_4, pm24_32bit_1_inst_3, pm24_32bit_1_inst[14:12], pm24_32bit_1_inst_2, pm24_32bit_1_inst[6:0]}),
    .Immediate(immediate_32bits_1_immediate));
  RF24_32bit rf24_32bit_1 (
    .rdAddres(pm24_32bit_1_inst_2), .Clock(Clock), .rfwrEnable(RFwrEnable), .rdData(multiplexer_4_out),
    .rs1Addres(pm24_32bit_1_inst_3), .rs2Addres(pm24_32bit_1_inst_4), .rs1Data(rf24_32bit_1_rs1data),
    .rs2Data(WData));
  Multiplexer #(.Bits(32)) multiplexer_1 (
    .sel(branch_32bit_1_rs1_pc),
    .in_0({pm24_32bit_1_inst[31:25], pm24_32bit_1_inst_4, pm24_32bit_1_inst_3, pm24_32bit_1_inst[14:12], pm24_32bit_1_inst_2, pm24_32bit_1_inst[6:0]}),
    .in_1(rf24_32bit_1_rs1data), .out(multiplexer_1_out));
  Multiplexer #(.Bits(32)) multiplexer_2 (
    .sel(ImmReg), .in_0(WData), .in_1(immediate_32bits_1_immediate), .out(multiplexer_2_out));
  Branch_32bit branch_32bit_1 (
    .UbrInst(cu_32bits_1_jal___jalr), .Function3(Function3), .BrInst(cu_32bits_1_branch), .R2Data(WData),
    .R1Data(rf24_32bit_1_rs1data), .PC_Jump(branch_32bit_1_pc_jump), .RS1_PC(branch_32bit_1_rs1_pc));  // open: Equal, LessThan, GreatOrEqual, LessThanU, GreatOrEqualU
  ALU_32bit alu_32bit_1 (
    .arg1(multiplexer_1_out), .arg2(multiplexer_2_out), .Funtion3(Function3), .Funtion7(SRAI_SUB),
    .Out(alu_32bit_1_out));
  Multiplexer #(.Bits(32)) multiplexer_3 (
    .sel(branch_32bit_1_pc_jump), .in_0(add_1_s), .in_1(alu_32bit_1_out), .out(multiplexer_3_out));
  DataMemory_32bits datamemory_32bits_1 (
    .WData(WData), .Clock(Clock), .DMwrEna(DMwrEn), .Function3(Function3), .RWAdress(alu_32bit_1_out),
    .DataRD(datamemory_32bits_1_datard));
  Multiplexer #(.Selector_Bits(2), .Bits(32)) multiplexer_4 (
    .sel(WBSel), .in_0(alu_32bit_1_out), .in_1(datamemory_32bits_1_datard), .in_2(add_1_s),
    .in_3(notconnected_1_out), .out(multiplexer_4_out));
  // NotConnected on notconnected_1_out
endmodule
