// Digital circuit RF24_32bit.dig as structural Verilog
module RF24_32bit (
  input  [4:0] rdAddres,
  input  Clock,
  input  rfwrEnable,
  input  [31:0] rdData,
  input  [4:0] rs1Addres,
  input  [4:0] rs2Addres,
  output [31:0] rs1Data,
  output [31:0] rs2Data
);

  wire comparator_1_eq, multiplexer_1_out;

  Comparator #(.Bits(5)) comparator_1 (.a({5{1'b0}}), .b(rdAddres), .eq(comparator_1_eq));  // open: gt, lt
  Multiplexer multiplexer_1 (.sel(comparator_1_eq), .in_0(rfwrEnable), .in_1(1'b0), .out(multiplexer_1_out));
  RegisterFile #(.AddrBits(5), .Bits(32)) registerfile_1 (
    .Din(rdData), .we(multiplexer_1_out), .Rw(rdAddres), .C(Clock), .Ra(rs1Addres), .Rb(rs2Addres),
    .Da(rs1Data), .Db(rs2Data));

  // Notes on the sheet:
  //   Register File de 32 casillas de memoria
  //   cada una de 32 bits
endmodule
