// Digital circuit DUX1a4_1bit.dig as structural Verilog
module DUX1a4_1bit (
  input  A,
  input  B,
  input  D,
  output I0,
  output I1,
  output I2,
  output I3
);

  wire not_1_out, not_2_out;

  not not_1 (not_1_out, A);
  not not_2 (not_2_out, B);
  and and_1 (I0, not_1_out, not_2_out, D);
  and and_2 (I1, not_1_out, B, D);
  and and_3 (I2, A, not_2_out, D);
  and and_4 (I3, A, B, D);

  // Notes on the sheet:
  //   Demultiplexor 1  a 4 de 1bit
endmodule
