// Digital circuit Deco_32bit.dig as structural Verilog
module Deco_32bit (
  input  [31:0] Inst,
  output [6:0] OpCode,
  output [4:0] Read,
  output [2:0] Function3,
  output [4:0] RS1,
  output [4:0] Rs2,
  output [6:0] Function7
);


  assign Function3 = Inst[14:12];
  assign Function7 = Inst[31:25];
  assign OpCode = Inst[6:0];
  assign Read = Inst[11:7];
  assign RS1 = Inst[19:15];
  assign Rs2 = Inst[24:20];
endmodule
