// Digital circuit Inst_Decoder_B.dig as structural Verilog
module Inst_Decoder_B (
  input  [31:0] Instruction,
  output [31:0] Immediate
);

  BitExtender #(.inputBits(1), .outputBits(19)) bitextender_1 (.in(Instruction[31]), .out(Immediate[31:13]));
  // Pins of 1 and 32 bits meet at Instruction

  assign Immediate[12:0] = {Instruction[31], Instruction[7], Instruction[30:25], Instruction[11:8], 1'b0};
endmodule
