// Digital circuit Inst_Decoder_J.dig as structural Verilog
module Inst_Decoder_J (
  input  [31:0] Instruction,
  output [31:0] Immediate
);

  wire [18:11] bitextender_1_out;

  BitExtender #(.inputBits(1), .outputBits(19)) bitextender_1 (
    .in(Instruction[31]), .out({bitextender_1_out, Immediate[31:21]}));
  // Pins of 11 and 19 bits meet at {bitextender_1_out, Immediate[31:21]}

  assign Immediate[20:1] = {Instruction[31], Instruction[19:12], Instruction[20], Instruction[30:21]};
endmodule
