// Digital circuit Inst_Decoder_S.dig as structural Verilog
module Inst_Decoder_S (
  input  [31:0] Instruction,
  output [31:0] Immediate
);

  BitExtender #(.inputBits(1), .outputBits(20)) bitextender_1 (.in(Instruction[31]), .out(Immediate[31:12]));

  assign Immediate[11:0] = {Instruction[31:25], Instruction[11:7]};
endmodule
