// Digital circuit Inst_Decoder_U.dig as structural Verilog
module Inst_Decoder_U (
  input  [31:0] Instruction,
  output [31:0] Immediate
);


  assign Immediate = {Instruction[31:12], {12{1'b0}}};
endmodule
