// Digital circuit MUX4a1_4bit.dig as structural Verilog
module MUX4a1_4bit (
  input  S0,
  input  S1,
  input  [3:0] I0,
  input  [3:0] I1,
  input  [3:0] I2,
  input  [3:0] I3,
  output [3:0] Y
);

  MUX4a1_1bit mux4a1_1bit_1 (.I0(I0[0]), .S0(S0), .S1(S1), .I1(I1[0]), .I2(I2[0]), .I3(I3[0]), .Y(Y[0]));
  MUX4a1_1bit mux4a1_1bit_2 (.I0(I0[1]), .S0(S0), .S1(S1), .I1(I1[1]), .I2(I2[1]), .I3(I3[1]), .Y(Y[1]));
  MUX4a1_1bit mux4a1_1bit_3 (.I0(I0[2]), .S0(S0), .S1(S1), .I1(I1[2]), .I2(I2[2]), .I3(I3[2]), .Y(Y[2]));
  MUX4a1_1bit mux4a1_1bit_4 (.I0(I0[3]), .S0(S0), .S1(S1), .I1(I1[3]), .I2(I2[3]), .I3(I3[3]), .Y(Y[3]));

  // Notes on the sheet:
  //   Multiplexor de 4bits
  //   0
  //   2
  //   3
  //   4
endmodule
