// Digital circuit Res4bit.dig as structural Verilog
module Res4bit (
  input  [3:0] A,
  input  [3:0] B,
  input  Bin,
  output [3:0] D,
  output Bout
);

  wire sum4bit_1_cout;
  wire [3:0] not_1_out;

  assign not_1_out = ~B;  // Not not_1, 4 bits wide
  Sum4bit sum4bit_1 (.A(A), .B(not_1_out), .Cin(Bin), .S(D), .Cout(sum4bit_1_cout));
  not not_2 (Bout, sum4bit_1_cout);

  // Notes on the sheet:
  //   Restador de 4 bits
endmodule
