// Digital circuit ResCom.dig as structural Verilog
module ResCom (
  input  A,
  input  B,
  input  Cin,
  output D,
  output Bo
);

  wire and_1_out, and_2_out, not_1_out, not_2_out, xor_1_out;

  not not_1 (not_1_out, A);
  xor xor_1 (xor_1_out, A, B);
  and and_1 (and_1_out, B, not_1_out);
  not not_2 (not_2_out, xor_1_out);
  xor xor_2 (D, xor_1_out, Cin);
  and and_2 (and_2_out, not_2_out, Cin);
  xor xor_3 (Bo, and_2_out, and_1_out);

  // Notes on the sheet:
  //   Restador Completo
endmodule
