// Digital circuit PC_32bit.dig as structural Verilog
module PC_32bit (
  input  [31:0] Input,
  input  Clock,
  input  WriteEnable,
  input  Reset,
  output [31:0] Output
);

  wire or_1_out;
  wire [31:0] multiplexer_1_out, multiplexer_2_out;

  Multiplexer #(.Bits(32)) multiplexer_1 (.sel(WriteEnable), .in_0(Output), .in_1(Input), .out(multiplexer_1_out));
  Multiplexer #(.Bits(32)) multiplexer_2 (
    .sel(Reset), .in_0(multiplexer_1_out), .in_1({32{1'b0}}), .out(multiplexer_2_out));
  or or_1 (or_1_out, WriteEnable, Reset);
  Register #(.Bits(32)) register_1 (.D(multiplexer_2_out), .C(Clock), .en(or_1_out), .Q(Output));

  // Notes on the sheet:
  //   Program Counter de 32bits
endmodule
