// Digital circuit RF24_32bit.dig as structural Verilog
module RF24_32bit (
  input  [23:0] rdAddres,
  input  Clock,
  input  rfwrEnable,
  input  [31:0] rdData,
  input  [23:0] rs1Addres,
  input  [23:0] rs2Addres,
  output [31:0] rs1Data,
  output [31:0] rs2Data
);

  wire comparator_1_eq, multiplexer_1_out;

  Comparator #(.Bits(24)) comparator_1 (.a({24{1'b0}}), .b(rdAddres), .eq(comparator_1_eq));  // open: gt, lt
  Multiplexer multiplexer_1 (.sel(comparator_1_eq), .in_0(rfwrEnable), .in_1(1'b0), .out(multiplexer_1_out));
  RegisterFile #(.AddrBits(24), .Bits(32)) registerfile_1 (
    .Din(rdData), .we(multiplexer_1_out), .Rw(rdAddres), .C(Clock), .Ra(rs1Addres), .Rb(rs2Addres),
    .Da(rs1Data), .Db(rs2Data));
endmodule
