// Digital circuit PruebaDeIntegraciónPC,PM,RF_32bits.dig as structural Verilog
module \PruebaDeIntegraciónPC_PM_RF_32bits  (
  input  Reset,
  input  Clock,
  input  WriteEnable,
  input  RFWriteEnable,
  input  [2:0] Operation,
  input  Des,
  output [6:0] Wa
);

  wire [31:0] alu_32bits_1_p5, notconnected_1_out, pc_32bit_1_output, rf24_32bit_1_rs1data,
       rf24_32bit_1_rs2data;
  wire [31:7] pm24_32bit_1_inst;

  PC_32bit pc_32bit_1 (
    .Input(notconnected_1_out), .Clock(Clock), .WriteEnable(WriteEnable), .Reset(Reset),
    .Output(pc_32bit_1_output));
  // NotConnected on notconnected_1_out
  PM24_32bit pm24_32bit_1 (.Addres(pc_32bit_1_output), .Inst({pm24_32bit_1_inst, Wa}));
  // Probe on pm24_32bit_1_inst[14:12]
  // Probe on pm24_32bit_1_inst[31:25]
  RF24_32bit rf24_32bit_1 (
    .rdAddres(pm24_32bit_1_inst[11:7]), .Clock(Clock), .rfwrEnable(RFWriteEnable), .rdData(alu_32bits_1_p5),
    .rs1Addres(pm24_32bit_1_inst[19:15]), .rs2Addres(pm24_32bit_1_inst[24:20]),
    .rs1Data(rf24_32bit_1_rs1data), .rs2Data(rf24_32bit_1_rs2data));
  // ALU_32bits alu_32bits_1: pin names not known; wires that end beside it: rf24_32bit_1_rs1data, rf24_32bit_1_rs2data, Operation, Des, alu_32bits_1_p5

  // Other names for the same wires on the sheet: CLK = Clock
endmodule
